// Logisim project testing_input_mode.circ as structural Verilog: 1 circuit, main circuit main
module main (
);

  wire _0_out, _1_out, and_1_out, and_3_out, button_1_out, clock_1_out, not_1_out, not_2_out, not_4_out,
       or_1_out, register_1_q, shift_register_1_out, shift_register_1_q0, waiting_q, xor_1_out;

  Button button_1 (.out(button_1_out));
  Clock clock_1 (.out(clock_1_out));
  not not_1 (not_1_out, waiting_q);
  LED led_1 (.in(waiting_q));
  Button _0 (.out(_0_out));
  Button _1 (.out(_1_out));
  Shift_Register #(.length(4)) shift_register_1 (
    .shift(not_1_out), .in(shift_register_1_out), .clk(clock_1_out), .out(shift_register_1_out),
    .load(button_1_out), .d0(1'b0), .q0(shift_register_1_q0), .d1(1'b0), .d2(1'b0), .d3(1'b1));  // open: clr, q1, q2, q3
  and and_1 (and_1_out, shift_register_1_q0, not_2_out);
  T_Flip_Flop waiting (.clk(or_1_out), .T(1'b1), .Q(waiting_q));  // open: Qn, preset, reset, en
  not not_2 (not_2_out, xor_1_out);
  or or_1 (or_1_out, and_1_out, and_3_out);
  xor xor_1 (xor_1_out, _0_out, _1_out);
  // AND_Gate and_2 is placed but not wired
  // OR_Gate or_2 is placed but not wired
  // NOT_Gate not_3 is placed but not wired
  and and_3 (and_3_out, not_4_out, waiting_q);
  not not_4 (not_4_out, xor_1_out);
  Register #(.width(1)) register_1 (.D(_1_out), .en(waiting_q), .Q(register_1_q), .clk(xor_1_out));  // open: clr
endmodule
